// Logisim project Design_Project_FA21_Ver_1.circ as structural Verilog: 7 circuits, main circuit main
module main (
  input  in_1,
  input  set_to_1,
  output [6:0] out_3,
  output out_4
);

  wire and_1_out, CLK, flipdetector_1_flip_detector;
  wire [1:0] count_3_flips_1_q2;
  wire [6:0] switchcircuit_1_channel_out;

  Clock clock_1 (.out(CLK));
  Keyboard keyboard_1 (.clk(CLK), .re(set_to_1), .clr(in_1), .avail(out_4), .data(out_3));
  LED led_1 (.in(out_4));
  flipDetector flipdetector_1 (
    .in_1(out_3), .Reset(in_1), .Enable(set_to_1), .CLK(CLK), .Flip_detector(flipdetector_1_flip_detector));
  LED led_2 (.in(flipdetector_1_flip_detector));
  SwitchCircuit switchcircuit_1 (
    .Channel_IN(out_3), .flip(flipdetector_1_flip_detector), .CLK(CLK), .Reset(in_1),
    .Channel_OUT(switchcircuit_1_channel_out));
  TTY #(.cols(80)) tty_1 (.data(out_3), .clk(CLK), .we(set_to_1), .clr(in_1));
  TTY #(.cols(80)) tty_2 (.data(switchcircuit_1_channel_out), .clk(CLK), .we(set_to_1), .clr(in_1));
  count_3_FLIPS count_3_flips_1 (
    .flip_IN(flipdetector_1_flip_detector), .CLK(CLK), .RESET(in_1), .q1(count_3_flips_1_q2[1]),
    .q2(count_3_flips_1_q2[0]));
  Hex_Digit_Display hex_digit_display_1 (.value({2'b00, count_3_flips_1_q2}));  // open: dp
  LED led_3 (.in(and_1_out));
  and and_1 (and_1_out, count_3_flips_1_q2[1], count_3_flips_1_q2[0]);

  // Other names for the same wires on the sheet: ENABLE = set_to_1; RESET = in_1

  // Notes on the sheet:
  //   Version 1
  //   set to 1 to read character
  //   System Clock
  //   set to 1 then back to 0
  //   set to 1 then back to 0 to empty buffer
  //   Keyboard
  //   Check Channel Bits
  //   Red Light is on at each " flip "
  //   set to 1 to write enable
  //   set to 1 then back to 0 to Clear Screen
  //   Normal Text
  //   Letters switched from lower case to upper case and viceversa
  //   Blue Light is On after 3 instances of a " flip "
endmodule

module SwitchCircuit (
  input  [6:0] Channel_IN,
  input  flip,
  input  CLK,
  input  Reset,
  output [6:0] Channel_OUT
);

  wire ENABLE;
  wire [6:0] bypass_1_1_channel_out, bypass_2_1_channel_out;

  T_Flip_Flop #(.trigger("falling")) t_ff_1 (.T(flip), .clk(CLK), .Q(ENABLE), .reset(Reset));  // open: Qn, preset
  Bypass_1 bypass_1_1 (.Channel_IN(Channel_IN), .Channel_OUT(bypass_1_1_channel_out));
  Bypass_2 bypass_2_1 (.Channel_IN(Channel_IN), .Channel_OUT(bypass_2_1_channel_out));
  Multiplexer #(.enable("false"), .width(7)) multiplexer_1 (
    .in0(bypass_2_1_channel_out), .in1(bypass_1_1_channel_out), .out(Channel_OUT), .sel(ENABLE));
endmodule

module flipDetector (
  input  [6:0] in_1,
  input  Reset,
  input  Enable,
  input  CLK,
  output Flip_detector
);

  wire and_1_out, and_2_out, and_3_out, and_4_out, and_5_out, and_6_out;
  wire [6:0] register_1_q, register_2_q, register_3_q, register_4_q, register_5_q, register_6_q;

  Register #(.width(7)) register_1 (.D(in_1), .en(Enable), .clk(CLK), .Q(register_1_q), .clr(Reset));
  and and_1 (and_1_out, ~register_1_q[6], register_1_q[5], ~register_1_q[4], ~register_1_q[3], ~register_1_q[2], ~register_1_q[1], ~register_1_q[0]);  // AND_Gate
  Register #(.width(7)) register_2 (.D(register_1_q), .en(Enable), .clk(CLK), .Q(register_2_q), .clr(Reset));
  Register #(.width(7)) register_3 (.D(register_2_q), .en(Enable), .clk(CLK), .Q(register_3_q), .clr(Reset));
  and and_2 (and_2_out, register_2_q[6], register_2_q[4], ~register_2_q[3], ~register_2_q[2], ~register_2_q[1], ~register_2_q[0]);  // AND_Gate
  Register #(.width(7)) register_4 (.D(register_3_q), .en(Enable), .clk(CLK), .Q(register_4_q), .clr(Reset));
  and and_3 (and_3_out, register_3_q[6], ~register_3_q[4], register_3_q[3], ~register_3_q[2], ~register_3_q[1], register_3_q[0]);  // AND_Gate
  Register #(.width(7)) register_5 (.D(register_4_q), .en(Enable), .clk(CLK), .Q(register_5_q), .clr(Reset));
  and and_4 (and_4_out, register_4_q[6], ~register_4_q[4], register_4_q[3], register_4_q[2], ~register_4_q[1], ~register_4_q[0]);  // AND_Gate
  and and_5 (and_5_out, register_5_q[6], ~register_5_q[4], ~register_5_q[3], register_5_q[2], register_5_q[1], ~register_5_q[0]);  // AND_Gate
  Register #(.width(7)) register_6 (.D(register_5_q), .en(Enable), .clk(CLK), .Q(register_6_q), .clr(Reset));
  and and_6 (and_6_out, ~register_6_q[6], register_6_q[5], ~register_6_q[4], ~register_6_q[3], ~register_6_q[2], ~register_6_q[1], ~register_6_q[0]);  // AND_Gate
  and and_7 (Flip_detector, and_1_out, and_2_out, and_3_out, and_4_out, and_5_out, and_6_out);
endmodule

module count_3_FLIPS (
  input  flip_IN,
  input  CLK,
  input  RESET,
  output q1,
  output q2
);

  wire and_1_out, and_2_out, and_3_out, d_ff_2_qn, or_1_out, or_2_out, xor_1_out, xor_2_out;

  xor xor_1 (xor_1_out, q1, flip_IN);
  and and_1 (and_1_out, q1, flip_IN);
  xor xor_2 (xor_2_out, ~d_ff_2_qn, flip_IN);  // XOR_Gate
  and and_2 (and_2_out, q1, d_ff_2_qn);
  or or_1 (or_1_out, and_2_out, and_3_out);
  and and_3 (and_3_out, ~d_ff_2_qn, xor_1_out);  // AND_Gate
  or or_2 (or_2_out, and_1_out, xor_2_out);
  D_Flip_Flop d_ff_1 (.D(or_1_out), .clk(CLK), .Q(q1), .reset(RESET));  // open: Qn, preset
  D_Flip_Flop d_ff_2 (.D(or_2_out), .clk(CLK), .Q(q2), .Qn(d_ff_2_qn), .reset(RESET));  // open: preset
endmodule

module Dual_Comparator (
  input  [6:0] value,
  output Upper_A_Z,
  output Lower_A_Z,
  output SPACE
);

  wire Greater2, Greater4, Less1, Less3;

  Comparator #(.mode("unsigned"), .width(7)) comparator_1 (.a(value), .b(7'b1000001), .lt(Less1));  // open: gt, eq
  Comparator #(.mode("unsigned"), .width(7)) comparator_2 (.a(value), .b(7'b1011010), .gt(Greater2));  // open: eq, lt
  Comparator #(.mode("unsigned"), .width(7)) comparator_3 (.a(value), .b(7'b1100001), .lt(Less3));  // open: gt, eq
  Comparator #(.mode("unsigned"), .width(7)) comparator_4 (.a(value), .b(7'b1111010), .gt(Greater4));  // open: eq, lt
  Comparator #(.mode("unsigned"), .width(7)) comparator_5 (.a(value), .b(7'b0100000), .eq(SPACE));  // open: gt, lt
  LED led_1 (.in(Upper_A_Z));
  xnor xnor_1 (Upper_A_Z, Less1, Greater2);
  LED led_2 (.in(Lower_A_Z));
  xnor xnor_2 (Lower_A_Z, Less3, Greater4);

  // Other names for the same wires on the sheet: Other0 = Upper_A_Z; Other1 = Lower_A_Z
endmodule

module Bypass_1 (
  input  [6:0] Channel_IN,
  output [6:0] Channel_OUT
);

  wire comparator_1_gt, comparator_1_lt, dual_comparator_1_lower_a_z, dual_comparator_1_space,
       dual_comparator_1_upper_a_z, not_1_out, not_2_out, xor_1_out;
  wire [2:0] subtractor_1_bout;
  wire [6:0] adder_1_out, multiplexer_1_out, subtractor_1_out;

  Comparator #(.mode("unsigned"), .width(7)) comparator_1 (
    .a(Channel_IN), .b(7'b1100000), .gt(comparator_1_gt), .lt(comparator_1_lt));  // open: eq
  Comparator #(.mode("unsigned"), .width(7)) comparator_2 (
    .a(Channel_IN), .b(7'b0100000), .eq(subtractor_1_bout[2]));  // open: gt, lt
  Dual_Comparator dual_comparator_1 (
    .value(Channel_IN), .Upper_A_Z(dual_comparator_1_upper_a_z), .Lower_A_Z(dual_comparator_1_lower_a_z),
    .SPACE(dual_comparator_1_space));
  not not_1 (not_1_out, comparator_1_gt);
  not not_2 (not_2_out, comparator_1_lt);
  ExactlyOne xor_1 (
    .out(xor_1_out), .in0(dual_comparator_1_upper_a_z), .in1(dual_comparator_1_lower_a_z),
    .in2(dual_comparator_1_space));
  Subtractor #(.width(7)) subtractor_1 (
    .a(Channel_IN), .b(7'b0100000), .out(subtractor_1_out), .bin(not_1_out), .bout(subtractor_1_bout[0]));
  Adder #(.width(7)) adder_1 (
    .a(Channel_IN), .b(7'b0100000), .out(adder_1_out), .cin(not_2_out), .cout(subtractor_1_bout[1]));
  Multiplexer #(.enable("false"), .select(3), .width(7)) multiplexer_1 (
    .in0(adder_1_out), .in1({7{1'b0}}), .in2(subtractor_1_out), .in3({7{1'b0}}), .in4({7{1'b0}}),
    .in5(7'b0100000), .in6({7{1'b0}}), .in7({7{1'b0}}), .out(multiplexer_1_out), .sel(subtractor_1_bout));
  // Probe on subtractor_1_bout
  Multiplexer #(.enable("false"), .width(7)) multiplexer_2 (
    .in0({7{1'b0}}), .in1(multiplexer_1_out), .out(Channel_OUT), .sel(xor_1_out));
endmodule

module Bypass_2 (
  input  [6:0] Channel_IN,
  output [6:0] Channel_OUT
);

  wire dual_comparator_1_lower_a_z, dual_comparator_1_space, dual_comparator_1_upper_a_z, xnor_1_out;

  Dual_Comparator dual_comparator_1 (
    .value(Channel_IN), .Upper_A_Z(dual_comparator_1_upper_a_z), .Lower_A_Z(dual_comparator_1_lower_a_z),
    .SPACE(dual_comparator_1_space));
  NotExactlyOne xnor_1 (
    .out(xnor_1_out), .in0(dual_comparator_1_upper_a_z), .in1(dual_comparator_1_lower_a_z),
    .in2(dual_comparator_1_space));
  Multiplexer #(.enable("false"), .width(7)) multiplexer_1 (
    .in0(Channel_IN), .in1({7{1'b0}}), .out(Channel_OUT), .sel(xnor_1_out));
endmodule
